# Fritzing sketch RFJoystick (saved by Fritzing 0.9.4)
breadboards: 1

parts:
  Part1 = Thumb Joystick
  RFduinoSMD1 = RFduino SMD
  LED1 = LED - 5mm [color="Red (633nm)" package="5 mm [THT]"]
  R1 = Resistor [tolerance=±5% resistance=220 package=THT]
  VCC1 = Battery

nets:
  GND: Part1.GND, RFduinoSMD1.gnd, R1.Pin_0
  N1: Part1.HORZ, RFduinoSMD1.gpio2
  N2: Part1.VERT, RFduinoSMD1.gpio3
  N3: RFduinoSMD1.vin, VCC1.+
  N4: RFduinoSMD1.gpio6, LED1.cathode
  N5: LED1.anode, R1.Pin_1
